# Fritzing sketch yellow_heat_schematic (saved by Fritzing 0.9.3b)
breadboards: 1

parts:
  ESP32_DevKit_C = lolin
  R1 = Resistor [tolerance=±5% resistance=1k package="2512 [SMD]"]
  R2 = Resistor [tolerance=±5% resistance=2.2k package="2512 [SMD]"]
  24VDC_to_3_3VDC = RioRand LM2596
  Burner = DC Power [voltage=24V]
  AC_Power = Power plug
  AC/DC_12V_0_167A_2W = RAC0x-SC [package=own]
  12V_to_5V_DC = RioRand LM2596
  Magnetic_Fuel_Level_Sensor = HALL-EFFECT [package=sc70]
  DS1 = DS18B20 1-Wire Temperature Sensor [part_number=DS18B20]
  S1 = SWITCH-MOMENTARY-2 [package=tactile_switch_smd-2]
  NEOPIXEL1 = Neopixel Strip -- White (60/m) [part_number=1138]

nets:
  N1: ESP32_DevKit_C.connector5, R1.Pin_0, R2.Pin_0
  N2: ESP32_DevKit_C.connector16, 12V_to_5V_DC.Pin_2
  N3: ESP32_DevKit_C.connector17, 12V_to_5V_DC.Pin_3, DS1.GND
  N4: ESP32_DevKit_C.connector19, NEOPIXEL1.DI
  GND: ESP32_DevKit_C.connector20, R2.Pin_1, 24VDC_to_3_3VDC.Pin_1, Magnetic_Fuel_Level_Sensor.GND, NEOPIXEL1.GND
  N5: ESP32_DevKit_C.connector22, S1.2
  N6: ESP32_DevKit_C.connector25, S1.1
  N7: ESP32_DevKit_C.connector27, 24VDC_to_3_3VDC.Pin_0
  N8: ESP32_DevKit_C.connector32, DS1.DQ
  N9: R1.Pin_1, Magnetic_Fuel_Level_Sensor.OUT
  N10: 24VDC_to_3_3VDC.Pin_2, Burner.V+
  N11: 24VDC_to_3_3VDC.Pin_3, Burner.V-
  N12: AC_Power.GND, AC/DC_12V_0_167A_2W.N
  N13: AC_Power.VCC, AC/DC_12V_0_167A_2W.L
  N14: AC/DC_12V_0_167A_2W.-, 12V_to_5V_DC.Pin_1
  N15: AC/DC_12V_0_167A_2W.+, 12V_to_5V_DC.Pin_0, Magnetic_Fuel_Level_Sensor.VCC
  VDD: DS1.VDD, NEOPIXEL1.+5V

custom parts:
  RAC0x-SC: The RAC01-SC and RAC02-SC series are ultra-compact universal input AC/DC power modules for PCB mounting. They feature high efficiency, low standby power, high operating temperature, soft start and short-circuit protection as well as a built-in EMC Class B filter. Output voltages range from 3.3VDC to 24VDC.
  Neopixel Strip -- White (60/m): Neopixel Strip, White, 60 pixels per meter.
